// Logisim project Part3.circ as structural Verilog: 1 circuit, main circuit main
module main (
  input  x,
  input  s,
  input  y,
  input  a,
  input  b,
  input  c,
  output f1,
  output f2
);

  wire and_1_out, and_2_out, and_3_out, not_1_out, not_2_out, not_3_out, or_1_out;

  not not_1 (not_1_out, s);
  or or_1 (or_1_out, a, b);
  not not_2 (not_2_out, b);
  and and_1 (and_1_out, x, not_1_out);
  and and_2 (and_2_out, s, y);
  not not_3 (not_3_out, or_1_out);
  and and_3 (and_3_out, not_2_out, c);
  or or_2 (f1, and_1_out, and_2_out);
  or or_3 (f2, not_3_out, and_3_out);

  // Notes on the sheet:
  //   Part I
  //   Part II
endmodule
