// Logisim project mux.circ as structural Verilog: 11 circuits, main circuit main
module main (
  input  SW_0,
  input  SW_1,
  input  SW_9,
  output LEDR_9
);

  mux2to1 u (.x(SW_0), .y(SW_1), .s(SW_9), .m(LEDR_9));
endmodule

module mux2to1 (
  input  x,
  input  y,
  input  s,
  output m
);

  Multiplexer #(.enable("false")) multiplexer_1 (.in0(x), .in1(y), .out(m), .sel(s));
endmodule

module mux4to1 (
  input  s1,
  input  s0,
  input  u,
  input  v,
  input  w,
  input  x,
  output m
);

  wire mux2to1_1_m, mux2to1_2_m;

  mux2to1 mux2to1_1 (.x(u), .y(v), .s(s0), .m(mux2to1_1_m));
  mux2to1 mux2to1_2 (.x(w), .y(x), .s(s0), .m(mux2to1_2_m));
  mux2to1 mux2to1_3 (.x(mux2to1_1_m), .y(mux2to1_2_m), .s(s1), .m(m));
endmodule

module HEXdecoder (
  input  c0,
  input  c1,
  input  c2,
  input  c3
);

  wire fivedecoder_1_x, fourdecoder_1_x, onedecoder_1_x, sixdecoder_1_x, threedecoder_1_x, twodecoder_1_x,
       zerodecoder_1_x;

  zeroDecoder zerodecoder_1 (.c0(c0), .c1(c1), .c2(c2), .c3(c3), .x(zerodecoder_1_x));
  oneDecoder onedecoder_1 (.c0(c0), .c1(c1), .c2(c2), .c3(c3), .x(onedecoder_1_x));
  twoDecoder twodecoder_1 (.c0(c0), .c1(c1), .c2(c2), .c3(c3), .x(twodecoder_1_x));
  threeDecoder threedecoder_1 (.c0(c0), .c1(c1), .c2(c2), .c3(c3), .x(threedecoder_1_x));
  fourDecoder fourdecoder_1 (.c0(c0), .c1(c1), .c2(c2), .c3(c3), .x(fourdecoder_1_x));
  fiveDecoder fivedecoder_1 (.c0(c0), .c1(c1), .c2(c2), .c3(c3), .x(fivedecoder_1_x));
  sixDecoder sixdecoder_1 (.c0(c0), .c1(c1), .c2(c2), .c3(c3), .x(sixdecoder_1_x));
  _7_Segment_Display display (
    .g(sixdecoder_1_x), .f(fivedecoder_1_x), .a(zerodecoder_1_x), .b(onedecoder_1_x), .e(fourdecoder_1_x),
    .d(threedecoder_1_x), .c(twodecoder_1_x));  // open: dp
endmodule

module zeroDecoder (
  input  c0,
  input  c1,
  input  c2,
  input  c3,
  output x
);

  wire and_1_out, and_2_out, and_3_out, and_4_out, and_5_out, and_6_out, not_1_out, not_2_out, not_3_out,
       not_4_out;

  not not_1 (not_1_out, c0);
  not not_2 (not_2_out, c1);
  not not_3 (not_3_out, c2);
  not not_4 (not_4_out, c3);
  and and_1 (and_1_out, not_3_out, not_1_out);
  and and_2 (and_2_out, not_4_out, c1);
  and and_3 (and_3_out, not_4_out, c2, c0);
  and and_4 (and_4_out, c2, c1);
  and and_5 (and_5_out, c3, not_1_out);
  and and_6 (and_6_out, c3, not_3_out, not_2_out);
  or or_1 (x, and_1_out, and_2_out, and_3_out, and_4_out, and_5_out, and_6_out);
endmodule

module oneDecoder (
  input  c0,
  input  c1,
  input  c2,
  input  c3,
  output x
);

  wire and_1_out, and_2_out, and_3_out, and_4_out, and_5_out, not_1_out, not_2_out, not_3_out, not_4_out;

  not not_1 (not_1_out, c0);
  not not_2 (not_2_out, c1);
  not not_3 (not_3_out, c2);
  not not_4 (not_4_out, c3);
  and and_1 (and_1_out, not_4_out, not_2_out, not_1_out);
  and and_2 (and_2_out, not_4_out, c1, c0);
  and and_3 (and_3_out, not_4_out, not_3_out);
  and and_4 (and_4_out, c3, not_2_out, c0);
  and and_5 (and_5_out, c3, not_3_out, not_1_out);
  or or_1 (x, and_1_out, and_2_out, and_3_out, and_4_out, and_5_out);
endmodule

module twoDecoder (
  input  c0,
  input  c1,
  input  c2,
  input  c3,
  output x
);

  wire and_1_out, and_2_out, and_3_out, and_4_out, and_5_out, not_1_out, not_2_out, not_3_out, not_4_out;

  not not_1 (not_1_out, c0);
  not not_2 (not_2_out, c1);
  not not_3 (not_3_out, c2);
  not not_4 (not_4_out, c3);
  and and_1 (and_1_out, not_4_out, not_2_out, not_1_out);
  and and_2 (and_2_out, not_4_out, c1, c0);
  and and_3 (and_3_out, not_4_out, c2, c1);
  and and_4 (and_4_out, not_2_out, c0);
  and and_5 (and_5_out, c3, not_3_out);
  or or_1 (x, and_1_out, and_2_out, and_3_out, and_4_out, and_5_out);
endmodule

module threeDecoder (
  input  c0,
  input  c1,
  input  c2,
  input  c3,
  output x
);

  wire and_1_out, and_2_out, and_3_out, and_4_out, and_5_out, not_1_out, not_2_out, not_3_out, not_4_out;

  not not_1 (not_1_out, c0);
  not not_2 (not_2_out, c1);
  not not_3 (not_3_out, c2);
  not not_4 (not_4_out, c3);
  and and_1 (and_1_out, not_4_out, not_3_out, not_1_out);
  and and_2 (and_2_out, c2, not_2_out, c0);
  and and_3 (and_3_out, not_3_out, c1, c0);
  and and_4 (and_4_out, c2, c1, not_1_out);
  and and_5 (and_5_out, c3, not_2_out);
  or or_1 (x, and_1_out, and_2_out, and_3_out, and_4_out, and_5_out);
endmodule

module fourDecoder (
  input  c0,
  input  c1,
  input  c2,
  input  c3,
  output x
);

  wire and_1_out, and_2_out, and_3_out, and_4_out, not_1_out, not_2_out, not_3_out, not_4_out;

  not not_1 (not_1_out, c0);
  not not_2 (not_2_out, c1);
  not not_3 (not_3_out, c2);
  not not_4 (not_4_out, c3);
  and and_1 (and_1_out, not_3_out, not_2_out, not_1_out);
  and and_2 (and_2_out, c1, not_1_out);
  and and_3 (and_3_out, c3, c2);
  and and_4 (and_4_out, c3, c1);
  or or_1 (x, and_1_out, and_2_out, and_3_out, and_4_out);
endmodule

module fiveDecoder (
  input  c0,
  input  c1,
  input  c2,
  input  c3,
  output x
);

  wire and_1_out, and_2_out, and_3_out, and_4_out, and_5_out, not_1_out, not_2_out, not_3_out, not_4_out;

  not not_1 (not_1_out, c0);
  not not_2 (not_2_out, c1);
  not not_3 (not_3_out, c2);
  not not_4 (not_4_out, c3);
  and and_1 (and_1_out, not_4_out, c2, not_2_out);
  and and_2 (and_2_out, c2, c1, not_1_out);
  and and_3 (and_3_out, not_2_out, not_1_out);
  and and_4 (and_4_out, c3, not_3_out);
  and and_5 (and_5_out, c3, c1);
  or or_1 (x, and_1_out, and_2_out, and_3_out, and_4_out, and_5_out);
endmodule

module sixDecoder (
  input  c0,
  input  c1,
  input  c2,
  input  c3,
  output x
);

  wire and_1_out, and_2_out, and_3_out, and_4_out, and_5_out, not_1_out, not_2_out, not_3_out, not_4_out;

  not not_1 (not_1_out, c0);
  not not_2 (not_2_out, c1);
  not not_3 (not_3_out, c2);
  not not_4 (not_4_out, c3);
  and and_1 (and_1_out, not_4_out, c2, not_2_out);
  and and_2 (and_2_out, c3, c2, c0);
  and and_3 (and_3_out, not_4_out, not_3_out, c1);
  and and_4 (and_4_out, c3, not_3_out);
  and and_5 (and_5_out, c1, not_1_out);
  or or_1 (x, and_1_out, and_2_out, and_3_out, and_4_out, and_5_out);
endmodule
