// Logisim project Part1.circ as structural Verilog: 1 circuit, main circuit main
module main (
  input  [9:0] cin,
  output cout
);

  Multiplexer #(.enable("false"), .select(3)) multiplexer_1 (
    .in0(cin[0]), .in1(cin[1]), .in2(cin[2]), .in3(cin[3]), .in4(cin[4]), .in5(cin[5]), .in6(cin[6]),
    .in7(1'b0), .out(cout), .sel(cin[9:7]));
endmodule
