// Logisim project Part2.circ as structural Verilog: 2 circuits, main circuit main
module main (
  input  [3:0] A,
  input  [3:0] B,
  input  cin,
  output [3:0] S,
  output cout
);

  wire fulladder_1_c0, fulladder_2_c0, fulladder_3_c0;

  FullAdder fulladder_1 (.ci(cin), .a(A[0]), .b(B[0]), .s(S[0]), .c0(fulladder_1_c0));
  FullAdder fulladder_2 (.ci(fulladder_1_c0), .a(A[1]), .b(B[1]), .s(S[1]), .c0(fulladder_2_c0));
  FullAdder fulladder_3 (.ci(fulladder_2_c0), .a(A[2]), .b(B[2]), .s(S[2]), .c0(fulladder_3_c0));
  FullAdder fulladder_4 (.ci(fulladder_3_c0), .a(A[3]), .b(B[3]), .s(S[3]), .c0(cout));
endmodule

module FullAdder (
  input  ci,
  input  a,
  input  b,
  output s,
  output c0
);

  wire xor_1_out;

  xor xor_1 (xor_1_out, a, b);
  Multiplexer #(.enable("false")) multiplexer_1 (.in0(b), .in1(ci), .out(c0), .sel(xor_1_out));
  xor xor_2 (s, ci, xor_1_out);
endmodule
