// Logisim project Part1.circ as structural Verilog
module DLatch (
  input  D,
  input  Clk,
  output Q,
  output QBar
);

  wire nand_1_out, nand_2_out, not_1_out;

  not not_1 (not_1_out, D);
  nand nand_1 (nand_1_out, D, Clk);
  nand nand_2 (nand_2_out, Clk, not_1_out);
  nand nand_3 (Q, nand_1_out, QBar);
  nand nand_4 (QBar, Q, nand_2_out);
endmodule

module MasterSlave (
  input  D,
  input  Clk,
  output Q
);

  wire dlatch_1_q, not_1_out;

  not not_1 (not_1_out, Clk);
  DLatch dlatch_1 (.D(D), .Clk(Clk), .Q(dlatch_1_q));  // open: QBar
  DLatch dlatch_2 (.D(dlatch_1_q), .Clk(not_1_out), .Q(Q));  // open: QBar
endmodule
