// Logisim project Part2.circ as structural Verilog
module ALU (
  input  [3:0] A,
  input  [2:0] func,
  output [7:0] ALUout
);

  wire Clk_out, hexdecoder_1_five, hexdecoder_1_four, hexdecoder_1_one, hexdecoder_1_six, hexdecoder_1_three,
       hexdecoder_1_two, hexdecoder_1_zero, hexdecoder_2_five, hexdecoder_2_four, hexdecoder_2_one,
       hexdecoder_2_six, hexdecoder_2_three, hexdecoder_2_two, hexdecoder_2_zero, hexdecoder_3_five,
       hexdecoder_3_four, hexdecoder_3_one, hexdecoder_3_six, hexdecoder_3_three, hexdecoder_3_two,
       hexdecoder_3_zero, hexdecoder_4_five, hexdecoder_4_four, hexdecoder_4_one, hexdecoder_4_six,
       hexdecoder_4_three, hexdecoder_4_two, hexdecoder_4_zero, not_1_out;
  wire [7:0] five_1_s, four_1_s, multiplexer_1_out, one_1_s, seven_1_s, six_1_s, three_1_s, two_1_s, zero_1_s;

  HEXdecoder hexdecoder_1 (
    .cin(A), .zero(hexdecoder_1_zero), .one(hexdecoder_1_one), .two(hexdecoder_1_two),
    .three(hexdecoder_1_three), .four(hexdecoder_1_four), .five(hexdecoder_1_five), .six(hexdecoder_1_six));
  _7_Segment_Display u_7_segment_display_1 (
    .g(hexdecoder_1_six), .f(hexdecoder_1_five), .a(hexdecoder_1_zero), .b(hexdecoder_1_one),
    .e(hexdecoder_1_four), .d(hexdecoder_1_three), .c(hexdecoder_1_two));  // open: dp
  zero zero_1 (.A(A), .S(zero_1_s));
  one one_1 (.A(A), .B(ALUout[3:0]), .S(one_1_s));
  two two_1 (.A(A), .B(ALUout[3:0]), .S(two_1_s));
  three three_1 (.A(A), .B(ALUout[3:0]), .S(three_1_s));
  four four_1 (.A(A), .B(ALUout[3:0]), .S(four_1_s));
  five five_1 (.A(A), .B(ALUout[3:0]), .S(five_1_s));
  six six_1 (.A(A), .B(ALUout[3:0]), .S(six_1_s));
  seven seven_1 (.A(A), .B(ALUout[3:0]), .S(seven_1_s));
  HEXdecoder hexdecoder_2 (
    .cin(ALUout[3:0]), .zero(hexdecoder_2_zero), .one(hexdecoder_2_one), .two(hexdecoder_2_two),
    .three(hexdecoder_2_three), .four(hexdecoder_2_four), .five(hexdecoder_2_five), .six(hexdecoder_2_six));
  _7_Segment_Display u_7_segment_display_2 (
    .g(hexdecoder_2_six), .f(hexdecoder_2_five), .a(hexdecoder_2_zero), .b(hexdecoder_2_one),
    .e(hexdecoder_2_four), .d(hexdecoder_2_three), .c(hexdecoder_2_two));  // open: dp
  Multiplexer #(.enable("false"), .select(3), .width(8)) multiplexer_1 (
    .in0(zero_1_s), .in1(one_1_s), .in2(two_1_s), .in3(three_1_s), .in4(four_1_s), .in5(five_1_s),
    .in6(six_1_s), .in7(seven_1_s), .out(multiplexer_1_out), .sel(func));
  Clock Clk (.out(Clk_out));
  Register register_1 (.D(multiplexer_1_out), .en(1'b1), .clk(Clk_out), .Q(ALUout), .clr(not_1_out));
  not not_1 (not_1_out, 1'b1);
  LED led_1 (.in(ALUout[0]));
  LED led_2 (.in(ALUout[1]));
  LED led_3 (.in(ALUout[2]));
  LED led_4 (.in(ALUout[3]));
  LED led_5 (.in(ALUout[4]));
  LED led_6 (.in(ALUout[5]));
  LED led_7 (.in(ALUout[6]));
  LED led_8 (.in(ALUout[7]));
  HEXdecoder hexdecoder_3 (
    .cin(ALUout[7:4]), .zero(hexdecoder_3_zero), .one(hexdecoder_3_one), .two(hexdecoder_3_two),
    .three(hexdecoder_3_three), .four(hexdecoder_3_four), .five(hexdecoder_3_five), .six(hexdecoder_3_six));
  _7_Segment_Display u_7_segment_display_3 (
    .g(hexdecoder_3_six), .f(hexdecoder_3_five), .a(hexdecoder_3_zero), .b(hexdecoder_3_one),
    .e(hexdecoder_3_four), .d(hexdecoder_3_three), .c(hexdecoder_3_two));  // open: dp
  HEXdecoder hexdecoder_4 (
    .cin(ALUout[3:0]), .zero(hexdecoder_4_zero), .one(hexdecoder_4_one), .two(hexdecoder_4_two),
    .three(hexdecoder_4_three), .four(hexdecoder_4_four), .five(hexdecoder_4_five), .six(hexdecoder_4_six));
  _7_Segment_Display u_7_segment_display_4 (
    .g(hexdecoder_4_six), .f(hexdecoder_4_five), .a(hexdecoder_4_zero), .b(hexdecoder_4_one),
    .e(hexdecoder_4_four), .d(hexdecoder_4_three), .c(hexdecoder_4_two));  // open: dp
endmodule

module zero (
  input  [3:0] A,
  output [7:0] S
);

  wire fulladder_1_c0, fulladder_2_c0, fulladder_3_c0;
  wire [4:0] fulladder_1_s;

  FullAdder fulladder_1 (.ci(1'b0), .a(A[0]), .b(1'b1), .s(fulladder_1_s[0]), .c0(fulladder_1_c0));
  FullAdder fulladder_2 (.ci(fulladder_1_c0), .a(A[1]), .b(1'b0), .s(fulladder_1_s[1]), .c0(fulladder_2_c0));
  FullAdder fulladder_3 (.ci(fulladder_2_c0), .a(A[2]), .b(1'b0), .s(fulladder_1_s[2]), .c0(fulladder_3_c0));
  FullAdder fulladder_4 (.ci(fulladder_3_c0), .a(A[3]), .b(1'b0), .s(fulladder_1_s[3]), .c0(fulladder_1_s[4]));
  assign S = {{3{1'b0}}, fulladder_1_s};  // Bit_Extender bit_extender_1
endmodule

module one (
  input  [3:0] A,
  input  [3:0] B,
  output [7:0] S
);

  wire fulladder_1_c0, fulladder_2_c0, fulladder_3_c0;
  wire [4:0] fulladder_1_s;

  FullAdder fulladder_1 (.ci(1'b0), .a(A[0]), .b(B[0]), .s(fulladder_1_s[0]), .c0(fulladder_1_c0));
  FullAdder fulladder_2 (.ci(fulladder_1_c0), .a(A[1]), .b(B[1]), .s(fulladder_1_s[1]), .c0(fulladder_2_c0));
  FullAdder fulladder_3 (.ci(fulladder_2_c0), .a(A[2]), .b(B[2]), .s(fulladder_1_s[2]), .c0(fulladder_3_c0));
  FullAdder fulladder_4 (.ci(fulladder_3_c0), .a(A[3]), .b(B[3]), .s(fulladder_1_s[3]), .c0(fulladder_1_s[4]));
  assign S = {{3{1'b0}}, fulladder_1_s};  // Bit_Extender bit_extender_1
endmodule

module two (
  input  [3:0] A,
  input  [3:0] B,
  output [7:0] S
);

  wire [3:0] adder_1_out;
  wire [4:4] adder_1_cout;

  Adder #(.width(4)) adder_1 (.a(A), .b(B), .out(adder_1_out), .cin(1'b0), .cout(adder_1_cout[4]));
  assign S = {{3{1'b0}}, {adder_1_cout[4], adder_1_out}};  // Bit_Extender bit_extender_1
endmodule

module three (
  input  [3:0] A,
  input  [3:0] B,
  output [7:0] S
);

  wire [3:0] or_1_out, xor_1_out;
  wire [4:0] bit_extender_1_out;
  wire [5:0] bit_extender_2_out;
  wire [6:0] bit_extender_3_out;

  assign or_1_out = A | B;  // OR_Gate or_1, 4 bits wide
  assign xor_1_out = A ^ B;  // XOR_Gate xor_1, 4 bits wide
  assign bit_extender_1_out = {{1{or_1_out[0]}}, xor_1_out};  // Bit_Extender bit_extender_1
  assign bit_extender_2_out = {{1{or_1_out[1]}}, bit_extender_1_out};  // Bit_Extender bit_extender_2
  assign bit_extender_3_out = {{1{or_1_out[2]}}, bit_extender_2_out};  // Bit_Extender bit_extender_3
  assign S = {{1{or_1_out[3]}}, bit_extender_3_out};  // Bit_Extender bit_extender_4
endmodule

module four (
  input  [3:0] A,
  input  [3:0] B,
  output [7:0] S
);

  wire or_1_out;

  or or_1 (or_1_out, A[0], A[1], A[2], A[3], B[0], B[1], B[2], B[3]);
  assign S = {{7{1'b0}}, or_1_out};  // Bit_Extender bit_extender_1
endmodule

module five (
  input  [3:0] A,
  input  [3:0] B,
  output [7:0] S
);

  wire [8:0] bit_extender_1_out;
  wire [8:8] shifter_1_out;

  assign bit_extender_1_out = {{5{1'b0}}, B};  // Bit_Extender bit_extender_1
  Shifter #(.width(9)) shifter_1 (.in(bit_extender_1_out), .\dist (A), .out({shifter_1_out[8], S}));
endmodule

module six (
  input  [3:0] A,
  input  [3:0] B,
  output [7:0] S
);

  wire [8:0] bit_extender_1_out;
  wire [8:8] shifter_1_out;

  assign bit_extender_1_out = {{5{1'b0}}, B};  // Bit_Extender bit_extender_1
  Shifter #(.shift("lr"), .width(9)) shifter_1 (.in(bit_extender_1_out), .\dist (A), .out({shifter_1_out[8], S}));
endmodule

module seven (
  input  [3:0] A,
  input  [3:0] B,
  output [7:0] S
);

  wire [3:0] multiplier_1_cout, multiplier_1_out;
  wire [4:0] bit_extender_1_out;
  wire [5:0] bit_extender_2_out;
  wire [6:0] bit_extender_3_out;

  Multiplier #(.width(4)) multiplier_1 (.a(A), .b(B), .out(multiplier_1_out), .cin(4'b0000), .cout(multiplier_1_cout));
  assign bit_extender_1_out = {{1{multiplier_1_cout[0]}}, multiplier_1_out};  // Bit_Extender bit_extender_1
  assign bit_extender_2_out = {{1{multiplier_1_cout[1]}}, bit_extender_1_out};  // Bit_Extender bit_extender_2
  assign bit_extender_3_out = {{1{multiplier_1_cout[2]}}, bit_extender_2_out};  // Bit_Extender bit_extender_3
  assign S = {{1{multiplier_1_cout[3]}}, bit_extender_3_out};  // Bit_Extender bit_extender_4
endmodule

module HEXdecoder (
  input  [3:0] cin,
  output zero,
  output one,
  output two,
  output three,
  output four,
  output five,
  output six
);

  zeroDecoder zerodecoder_1 (.c0(cin[0]), .c1(cin[1]), .c2(cin[2]), .c3(cin[3]), .x(zero));
  oneDecoder onedecoder_1 (.c0(cin[0]), .c1(cin[1]), .c2(cin[2]), .c3(cin[3]), .x(one));
  twoDecoder twodecoder_1 (.c0(cin[0]), .c1(cin[1]), .c2(cin[2]), .c3(cin[3]), .x(two));
  threeDecoder threedecoder_1 (.c0(cin[0]), .c1(cin[1]), .c2(cin[2]), .c3(cin[3]), .x(three));
  fourDecoder fourdecoder_1 (.c0(cin[0]), .c1(cin[1]), .c2(cin[2]), .c3(cin[3]), .x(four));
  fiveDecoder fivedecoder_1 (.c0(cin[0]), .c1(cin[1]), .c2(cin[2]), .c3(cin[3]), .x(five));
  sixDecoder sixdecoder_1 (.c0(cin[0]), .c1(cin[1]), .c2(cin[2]), .c3(cin[3]), .x(six));
endmodule

module zeroDecoder (
  input  c0,
  input  c1,
  input  c2,
  input  c3,
  output x
);

  wire and_1_out, and_2_out, and_3_out, and_4_out, and_5_out, and_6_out, not_1_out, not_2_out, not_3_out,
       not_4_out;

  not not_1 (not_1_out, c0);
  not not_2 (not_2_out, c1);
  not not_3 (not_3_out, c2);
  not not_4 (not_4_out, c3);
  and and_1 (and_1_out, not_3_out, not_1_out);
  and and_2 (and_2_out, not_4_out, c1);
  and and_3 (and_3_out, not_4_out, c2, c0);
  and and_4 (and_4_out, c2, c1);
  and and_5 (and_5_out, c3, not_1_out);
  and and_6 (and_6_out, c3, not_3_out, not_2_out);
  or or_1 (x, and_1_out, and_2_out, and_3_out, and_4_out, and_5_out, and_6_out);
endmodule

module oneDecoder (
  input  c0,
  input  c1,
  input  c2,
  input  c3,
  output x
);

  wire and_1_out, and_2_out, and_3_out, and_4_out, and_5_out, not_1_out, not_2_out, not_3_out, not_4_out;

  not not_1 (not_1_out, c0);
  not not_2 (not_2_out, c1);
  not not_3 (not_3_out, c2);
  not not_4 (not_4_out, c3);
  and and_1 (and_1_out, not_4_out, not_2_out, not_1_out);
  and and_2 (and_2_out, not_4_out, c1, c0);
  and and_3 (and_3_out, not_4_out, not_3_out);
  and and_4 (and_4_out, c3, not_2_out, c0);
  and and_5 (and_5_out, c3, not_3_out, not_1_out);
  or or_1 (x, and_1_out, and_2_out, and_3_out, and_4_out, and_5_out);
endmodule

module twoDecoder (
  input  c0,
  input  c1,
  input  c2,
  input  c3,
  output x
);

  wire and_1_out, and_2_out, and_3_out, and_4_out, and_5_out, not_1_out, not_2_out, not_3_out, not_4_out;

  not not_1 (not_1_out, c0);
  not not_2 (not_2_out, c1);
  not not_3 (not_3_out, c2);
  not not_4 (not_4_out, c3);
  and and_1 (and_1_out, not_4_out, not_2_out, not_1_out);
  and and_2 (and_2_out, not_4_out, c1, c0);
  and and_3 (and_3_out, not_4_out, c2, c1);
  and and_4 (and_4_out, not_2_out, c0);
  and and_5 (and_5_out, c3, not_3_out);
  or or_1 (x, and_1_out, and_2_out, and_3_out, and_4_out, and_5_out);
endmodule

module threeDecoder (
  input  c0,
  input  c1,
  input  c2,
  input  c3,
  output x
);

  wire and_1_out, and_2_out, and_3_out, and_4_out, and_5_out, not_1_out, not_2_out, not_3_out, not_4_out;

  not not_1 (not_1_out, c0);
  not not_2 (not_2_out, c1);
  not not_3 (not_3_out, c2);
  not not_4 (not_4_out, c3);
  and and_1 (and_1_out, not_4_out, not_3_out, not_1_out);
  and and_2 (and_2_out, c2, not_2_out, c0);
  and and_3 (and_3_out, not_3_out, c1, c0);
  and and_4 (and_4_out, c2, c1, not_1_out);
  and and_5 (and_5_out, c3, not_2_out);
  or or_1 (x, and_1_out, and_2_out, and_3_out, and_4_out, and_5_out);
endmodule

module fourDecoder (
  input  c0,
  input  c1,
  input  c2,
  input  c3,
  output x
);

  wire and_1_out, and_2_out, and_3_out, and_4_out, not_1_out, not_2_out, not_3_out, not_4_out;

  not not_1 (not_1_out, c0);
  not not_2 (not_2_out, c1);
  not not_3 (not_3_out, c2);
  not not_4 (not_4_out, c3);
  and and_1 (and_1_out, not_3_out, not_2_out, not_1_out);
  and and_2 (and_2_out, c1, not_1_out);
  and and_3 (and_3_out, c3, c2);
  and and_4 (and_4_out, c3, c1);
  or or_1 (x, and_1_out, and_2_out, and_3_out, and_4_out);
endmodule

module fiveDecoder (
  input  c0,
  input  c1,
  input  c2,
  input  c3,
  output x
);

  wire and_1_out, and_2_out, and_3_out, and_4_out, and_5_out, not_1_out, not_2_out, not_3_out, not_4_out;

  not not_1 (not_1_out, c0);
  not not_2 (not_2_out, c1);
  not not_3 (not_3_out, c2);
  not not_4 (not_4_out, c3);
  and and_1 (and_1_out, not_4_out, c2, not_2_out);
  and and_2 (and_2_out, c2, c1, not_1_out);
  and and_3 (and_3_out, not_2_out, not_1_out);
  and and_4 (and_4_out, c3, not_3_out);
  and and_5 (and_5_out, c3, c1);
  or or_1 (x, and_1_out, and_2_out, and_3_out, and_4_out, and_5_out);
endmodule

module sixDecoder (
  input  c0,
  input  c1,
  input  c2,
  input  c3,
  output x
);

  wire and_1_out, and_2_out, and_3_out, and_4_out, and_5_out, not_1_out, not_2_out, not_3_out, not_4_out;

  not not_1 (not_1_out, c0);
  not not_2 (not_2_out, c1);
  not not_3 (not_3_out, c2);
  not not_4 (not_4_out, c3);
  and and_1 (and_1_out, not_4_out, c2, not_2_out);
  and and_2 (and_2_out, c3, c2, c0);
  and and_3 (and_3_out, not_4_out, not_3_out, c1);
  and and_4 (and_4_out, c3, not_3_out);
  and and_5 (and_5_out, c1, not_1_out);
  or or_1 (x, and_1_out, and_2_out, and_3_out, and_4_out, and_5_out);
endmodule

module FullAdder (
  input  ci,
  input  a,
  input  b,
  output s,
  output c0
);

  wire xor_1_out;

  xor xor_1 (xor_1_out, a, b);
  Multiplexer #(.enable("false")) multiplexer_1 (.in0(b), .in1(ci), .out(c0), .sel(xor_1_out));
  xor xor_2 (s, ci, xor_1_out);
endmodule
