// Logisim project Part3.circ as structural Verilog
module OneBitShifter (
  input  load_val,
  input  cin,
  input  shift,
  input  Clk,
  input  load_n,
  input  reset,
  output cout
);

  wire mux2to1_1_m, mux2to1_2_m;

  mux2to1 mux2to1_1 (.x(cout), .y(cin), .s(shift), .m(mux2to1_1_m));
  mux2to1 mux2to1_2 (.x(load_val), .y(mux2to1_1_m), .s(load_n), .m(mux2to1_2_m));
  D_Flip_Flop d_ff_1 (.D(mux2to1_2_m), .clk(Clk), .Q(cout), .reset(reset));  // open: Qn, preset
endmodule

module mux2to1 (
  input  x,
  input  y,
  input  s,
  output m
);

  Multiplexer #(.enable("false")) multiplexer_1 (.in0(x), .in1(y), .out(m), .sel(s));
endmodule

module ShiftRegister (
  input  [7:0] load_val,
  input  ASR,
  input  reset,
  input  load_n,
  input  Clk,
  input  ShiftRight,
  output [7:0] Q
);

  wire onebitshifter_1_cout, signextender_1_cout, signextender_1_sign;

  signextender signextender_1 (
    .sign_in(onebitshifter_1_cout), .ASR(ASR), .sign(signextender_1_sign), .cout(signextender_1_cout),
    .sign_value(Q[7]));
  OneBitShifter onebitshifter_1 (
    .load_val(load_val[7]), .cin(signextender_1_sign), .shift(ShiftRight), .Clk(Clk), .load_n(load_n),
    .reset(reset), .cout(onebitshifter_1_cout));
  OneBitShifter onebitshifter_2 (
    .load_val(load_val[6]), .cin(signextender_1_cout), .shift(ShiftRight), .Clk(Clk), .load_n(load_n),
    .reset(reset), .cout(Q[6]));
  OneBitShifter onebitshifter_3 (
    .load_val(load_val[5]), .cin(Q[6]), .shift(ShiftRight), .Clk(Clk), .load_n(load_n), .reset(reset),
    .cout(Q[5]));
  OneBitShifter onebitshifter_4 (
    .load_val(load_val[4]), .cin(Q[5]), .shift(ShiftRight), .Clk(Clk), .load_n(load_n), .reset(reset),
    .cout(Q[4]));
  OneBitShifter onebitshifter_5 (
    .load_val(load_val[3]), .cin(Q[4]), .shift(ShiftRight), .Clk(Clk), .load_n(load_n), .reset(reset),
    .cout(Q[3]));
  OneBitShifter onebitshifter_6 (
    .load_val(load_val[2]), .cin(Q[3]), .shift(ShiftRight), .Clk(Clk), .load_n(load_n), .reset(reset),
    .cout(Q[2]));
  OneBitShifter onebitshifter_7 (
    .load_val(load_val[1]), .cin(Q[2]), .shift(ShiftRight), .Clk(Clk), .load_n(load_n), .reset(reset),
    .cout(Q[1]));
  OneBitShifter onebitshifter_8 (
    .load_val(load_val[0]), .cin(Q[1]), .shift(ShiftRight), .Clk(Clk), .load_n(load_n), .reset(reset),
    .cout(Q[0]));
endmodule

module signextender (
  input  sign_in,
  input  ASR,
  output sign,
  output cout,
  output sign_value
);

  mux2to1 mux2to1_1 (.x(1'b0), .y(sign_in), .s(ASR), .m(sign));
  mux2to1 mux2to1_2 (.x(sign_in), .y(1'b0), .s(ASR), .m(cout));

  assign sign_value = sign_in;
endmodule
