// Logisim project Part1.circ as structural Verilog: 9 circuits, main circuit main
module main (
  input  Enable,
  input  Clear_b,
  output cout
);

  wire and_1_out, and_2_out, and_3_out, and_4_out, and_5_out, and_6_out, and_7_out, Clk_out,
       hexdecoder_1_five, hexdecoder_1_four, hexdecoder_1_one, hexdecoder_1_six, hexdecoder_1_three,
       hexdecoder_1_two, hexdecoder_1_zero, hexdecoder_2_five, hexdecoder_2_four, hexdecoder_2_one,
       hexdecoder_2_six, hexdecoder_2_three, hexdecoder_2_two, hexdecoder_2_zero, not_1_out;
  wire [2:0] t_ff_5_q;
  wire [3:0] t_ff_1_q;

  Clock Clk (.out(Clk_out));
  T_Flip_Flop t_ff_1 (.T(Enable), .clk(Clk_out), .Q(t_ff_1_q[0]), .reset(not_1_out));  // open: Qn, preset
  not not_1 (not_1_out, Clear_b);
  and and_1 (and_1_out, Enable, t_ff_1_q[0]);
  T_Flip_Flop t_ff_2 (.T(and_1_out), .clk(Clk_out), .Q(t_ff_1_q[1]), .reset(not_1_out));  // open: Qn, preset
  and and_2 (and_2_out, and_1_out, t_ff_1_q[1]);
  HEXdecoder hexdecoder_1 (
    .cin(t_ff_1_q), .zero(hexdecoder_1_zero), .one(hexdecoder_1_one), .two(hexdecoder_1_two),
    .three(hexdecoder_1_three), .four(hexdecoder_1_four), .five(hexdecoder_1_five), .six(hexdecoder_1_six));
  T_Flip_Flop t_ff_3 (.T(and_2_out), .clk(Clk_out), .Q(t_ff_1_q[2]), .reset(not_1_out));  // open: Qn, preset
  _7_Segment_Display u_7_segment_display_1 (
    .g(hexdecoder_1_six), .f(hexdecoder_1_five), .a(hexdecoder_1_zero), .b(hexdecoder_1_one),
    .e(hexdecoder_1_four), .d(hexdecoder_1_three), .c(hexdecoder_1_two));  // open: dp
  and and_3 (and_3_out, and_2_out, t_ff_1_q[2]);
  T_Flip_Flop t_ff_4 (.T(and_3_out), .clk(Clk_out), .Q(t_ff_1_q[3]), .reset(not_1_out));  // open: Qn, preset
  and and_4 (and_4_out, and_3_out, t_ff_1_q[3]);
  T_Flip_Flop t_ff_5 (.T(and_4_out), .clk(Clk_out), .Q(t_ff_5_q[0]), .reset(not_1_out));  // open: Qn, preset
  and and_5 (and_5_out, and_4_out, t_ff_5_q[0]);
  T_Flip_Flop t_ff_6 (.T(and_5_out), .clk(Clk_out), .Q(t_ff_5_q[1]), .reset(not_1_out));  // open: Qn, preset
  and and_6 (and_6_out, and_5_out, t_ff_5_q[1]);
  T_Flip_Flop t_ff_7 (.T(and_6_out), .clk(Clk_out), .Q(t_ff_5_q[2]), .reset(not_1_out));  // open: Qn, preset
  HEXdecoder hexdecoder_2 (
    .cin({cout, t_ff_5_q}), .zero(hexdecoder_2_zero), .one(hexdecoder_2_one), .two(hexdecoder_2_two),
    .three(hexdecoder_2_three), .four(hexdecoder_2_four), .five(hexdecoder_2_five), .six(hexdecoder_2_six));
  and and_7 (and_7_out, and_6_out, t_ff_5_q[2]);
  T_Flip_Flop t_ff_8 (.T(and_7_out), .clk(Clk_out), .Q(cout), .reset(not_1_out));  // open: Qn, preset
  _7_Segment_Display u_7_segment_display_2 (
    .g(hexdecoder_2_six), .f(hexdecoder_2_five), .a(hexdecoder_2_zero), .b(hexdecoder_2_one),
    .e(hexdecoder_2_four), .d(hexdecoder_2_three), .c(hexdecoder_2_two));  // open: dp
endmodule

module HEXdecoder (
  input  [3:0] cin,
  output zero,
  output one,
  output two,
  output three,
  output four,
  output five,
  output six
);

  zeroDecoder zerodecoder_1 (.c0(cin[0]), .c1(cin[1]), .c2(cin[2]), .c3(cin[3]), .x(zero));
  oneDecoder onedecoder_1 (.c0(cin[0]), .c1(cin[1]), .c2(cin[2]), .c3(cin[3]), .x(one));
  twoDecoder twodecoder_1 (.c0(cin[0]), .c1(cin[1]), .c2(cin[2]), .c3(cin[3]), .x(two));
  threeDecoder threedecoder_1 (.c0(cin[0]), .c1(cin[1]), .c2(cin[2]), .c3(cin[3]), .x(three));
  fourDecoder fourdecoder_1 (.c0(cin[0]), .c1(cin[1]), .c2(cin[2]), .c3(cin[3]), .x(four));
  fiveDecoder fivedecoder_1 (.c0(cin[0]), .c1(cin[1]), .c2(cin[2]), .c3(cin[3]), .x(five));
  sixDecoder sixdecoder_1 (.c0(cin[0]), .c1(cin[1]), .c2(cin[2]), .c3(cin[3]), .x(six));
endmodule

module zeroDecoder (
  input  c0,
  input  c1,
  input  c2,
  input  c3,
  output x
);

  wire and_1_out, and_2_out, and_3_out, and_4_out, and_5_out, and_6_out, not_1_out, not_2_out, not_3_out,
       not_4_out;

  not not_1 (not_1_out, c0);
  not not_2 (not_2_out, c1);
  not not_3 (not_3_out, c2);
  not not_4 (not_4_out, c3);
  and and_1 (and_1_out, not_3_out, not_1_out);
  and and_2 (and_2_out, not_4_out, c1);
  and and_3 (and_3_out, not_4_out, c2, c0);
  and and_4 (and_4_out, c2, c1);
  and and_5 (and_5_out, c3, not_1_out);
  and and_6 (and_6_out, c3, not_3_out, not_2_out);
  or or_1 (x, and_1_out, and_2_out, and_3_out, and_4_out, and_5_out, and_6_out);
endmodule

module oneDecoder (
  input  c0,
  input  c1,
  input  c2,
  input  c3,
  output x
);

  wire and_1_out, and_2_out, and_3_out, and_4_out, and_5_out, not_1_out, not_2_out, not_3_out, not_4_out;

  not not_1 (not_1_out, c0);
  not not_2 (not_2_out, c1);
  not not_3 (not_3_out, c2);
  not not_4 (not_4_out, c3);
  and and_1 (and_1_out, not_4_out, not_2_out, not_1_out);
  and and_2 (and_2_out, not_4_out, c1, c0);
  and and_3 (and_3_out, not_4_out, not_3_out);
  and and_4 (and_4_out, c3, not_2_out, c0);
  and and_5 (and_5_out, c3, not_3_out, not_1_out);
  or or_1 (x, and_1_out, and_2_out, and_3_out, and_4_out, and_5_out);
endmodule

module twoDecoder (
  input  c0,
  input  c1,
  input  c2,
  input  c3,
  output x
);

  wire and_1_out, and_2_out, and_3_out, and_4_out, and_5_out, not_1_out, not_2_out, not_3_out, not_4_out;

  not not_1 (not_1_out, c0);
  not not_2 (not_2_out, c1);
  not not_3 (not_3_out, c2);
  not not_4 (not_4_out, c3);
  and and_1 (and_1_out, not_4_out, not_2_out, not_1_out);
  and and_2 (and_2_out, not_4_out, c1, c0);
  and and_3 (and_3_out, not_4_out, c2, c1);
  and and_4 (and_4_out, not_2_out, c0);
  and and_5 (and_5_out, c3, not_3_out);
  or or_1 (x, and_1_out, and_2_out, and_3_out, and_4_out, and_5_out);
endmodule

module threeDecoder (
  input  c0,
  input  c1,
  input  c2,
  input  c3,
  output x
);

  wire and_1_out, and_2_out, and_3_out, and_4_out, and_5_out, not_1_out, not_2_out, not_3_out, not_4_out;

  not not_1 (not_1_out, c0);
  not not_2 (not_2_out, c1);
  not not_3 (not_3_out, c2);
  not not_4 (not_4_out, c3);
  and and_1 (and_1_out, not_4_out, not_3_out, not_1_out);
  and and_2 (and_2_out, c2, not_2_out, c0);
  and and_3 (and_3_out, not_3_out, c1, c0);
  and and_4 (and_4_out, c2, c1, not_1_out);
  and and_5 (and_5_out, c3, not_2_out);
  or or_1 (x, and_1_out, and_2_out, and_3_out, and_4_out, and_5_out);
endmodule

module fourDecoder (
  input  c0,
  input  c1,
  input  c2,
  input  c3,
  output x
);

  wire and_1_out, and_2_out, and_3_out, and_4_out, not_1_out, not_2_out, not_3_out, not_4_out;

  not not_1 (not_1_out, c0);
  not not_2 (not_2_out, c1);
  not not_3 (not_3_out, c2);
  not not_4 (not_4_out, c3);
  and and_1 (and_1_out, not_3_out, not_2_out, not_1_out);
  and and_2 (and_2_out, c1, not_1_out);
  and and_3 (and_3_out, c3, c2);
  and and_4 (and_4_out, c3, c1);
  or or_1 (x, and_1_out, and_2_out, and_3_out, and_4_out);
endmodule

module fiveDecoder (
  input  c0,
  input  c1,
  input  c2,
  input  c3,
  output x
);

  wire and_1_out, and_2_out, and_3_out, and_4_out, and_5_out, not_1_out, not_2_out, not_3_out, not_4_out;

  not not_1 (not_1_out, c0);
  not not_2 (not_2_out, c1);
  not not_3 (not_3_out, c2);
  not not_4 (not_4_out, c3);
  and and_1 (and_1_out, not_4_out, c2, not_2_out);
  and and_2 (and_2_out, c2, c1, not_1_out);
  and and_3 (and_3_out, not_2_out, not_1_out);
  and and_4 (and_4_out, c3, not_3_out);
  and and_5 (and_5_out, c3, c1);
  or or_1 (x, and_1_out, and_2_out, and_3_out, and_4_out, and_5_out);
endmodule

module sixDecoder (
  input  c0,
  input  c1,
  input  c2,
  input  c3,
  output x
);

  wire and_1_out, and_2_out, and_3_out, and_4_out, and_5_out, not_1_out, not_2_out, not_3_out, not_4_out;

  not not_1 (not_1_out, c0);
  not not_2 (not_2_out, c1);
  not not_3 (not_3_out, c2);
  not not_4 (not_4_out, c3);
  and and_1 (and_1_out, not_4_out, c2, not_2_out);
  and and_2 (and_2_out, c3, c2, c0);
  and and_3 (and_3_out, not_4_out, not_3_out, c1);
  and and_4 (and_4_out, c3, not_3_out);
  and and_5 (and_5_out, c1, not_1_out);
  or or_1 (x, and_1_out, and_2_out, and_3_out, and_4_out, and_5_out);
endmodule
