// Logisim project Part2.circ as structural Verilog: 11 circuits, main circuit main
module main (
  input  SW0,
  input  clear,
  input  SW1
);

  wire Clk_out, hexdecoder_1_five, hexdecoder_1_four, hexdecoder_1_one, hexdecoder_1_six, hexdecoder_1_three,
       hexdecoder_1_two, hexdecoder_1_zero, ratedivider_1_clkout;
  wire [3:0] displaycounter_1_cout;

  Clock Clk (.out(Clk_out));
  RateDivider ratedivider_1 (.SW0(SW0), .SW1(SW1), .ClkIn(Clk_out), .ClkOut(ratedivider_1_clkout));
  DisplayCounter displaycounter_1 (.clear(clear), .enable(ratedivider_1_clkout), .cout(displaycounter_1_cout));
  HEXdecoder hexdecoder_1 (
    .cin(displaycounter_1_cout), .zero(hexdecoder_1_zero), .one(hexdecoder_1_one), .two(hexdecoder_1_two),
    .three(hexdecoder_1_three), .four(hexdecoder_1_four), .five(hexdecoder_1_five), .six(hexdecoder_1_six));
  _7_Segment_Display u_7_segment_display_1 (
    .g(hexdecoder_1_six), .f(hexdecoder_1_five), .a(hexdecoder_1_zero), .b(hexdecoder_1_one),
    .e(hexdecoder_1_four), .d(hexdecoder_1_three), .c(hexdecoder_1_two));  // open: dp
endmodule

module RateDivider (
  input  SW0,
  input  SW1,
  input  ClkIn,
  output ClkOut
);

  wire d_ff_1_q, d_ff_1_qn, d_ff_2_q, d_ff_2_qn, d_ff_3_q, d_ff_3_qn, d_ff_4_q, d_ff_4_qn, d_ff_5_q,
       d_ff_5_qn, d_ff_6_q, d_ff_6_qn;

  D_Flip_Flop d_ff_1 (.D(d_ff_1_qn), .clk(ClkIn), .Q(d_ff_1_q), .Qn(d_ff_1_qn));  // open: preset, reset
  D_Flip_Flop d_ff_2 (.D(d_ff_2_qn), .clk(d_ff_1_q), .Q(d_ff_2_q), .Qn(d_ff_2_qn));  // open: preset, reset
  D_Flip_Flop d_ff_3 (.D(d_ff_3_qn), .clk(d_ff_2_q), .Q(d_ff_3_q), .Qn(d_ff_3_qn));  // open: preset, reset
  D_Flip_Flop d_ff_4 (.D(d_ff_4_qn), .clk(d_ff_3_q), .Q(d_ff_4_q), .Qn(d_ff_4_qn));  // open: preset, reset
  D_Flip_Flop d_ff_5 (.D(d_ff_5_qn), .clk(d_ff_4_q), .Q(d_ff_5_q), .Qn(d_ff_5_qn));  // open: preset, reset
  D_Flip_Flop d_ff_6 (.D(d_ff_6_qn), .clk(d_ff_5_q), .Q(d_ff_6_q), .Qn(d_ff_6_qn));  // open: preset, reset
  Multiplexer #(.enable("false"), .select(2)) multiplexer_1 (
    .in0(ClkIn), .in1(d_ff_4_q), .in2(d_ff_5_q), .in3(d_ff_6_q), .out(ClkOut), .sel({SW1, SW0}));
endmodule

module DisplayCounter (
  input  clear,
  input  enable,
  output [3:0] cout
);

  wire not_1_out;

  Counter #(.max('hf), .width(4)) counter_1 (
    .clr(clear), .load(not_1_out), .up(1'b1), .clk(enable), .D(4'b0000), .Q(cout));  // open: count, carry
  not not_1 (not_1_out, 1'b1);
endmodule

module HEXdecoder (
  input  [3:0] cin,
  output zero,
  output one,
  output two,
  output three,
  output four,
  output five,
  output six
);

  zeroDecoder zerodecoder_1 (.c0(cin[0]), .c1(cin[1]), .c2(cin[2]), .c3(cin[3]), .x(zero));
  oneDecoder onedecoder_1 (.c0(cin[0]), .c1(cin[1]), .c2(cin[2]), .c3(cin[3]), .x(one));
  twoDecoder twodecoder_1 (.c0(cin[0]), .c1(cin[1]), .c2(cin[2]), .c3(cin[3]), .x(two));
  threeDecoder threedecoder_1 (.c0(cin[0]), .c1(cin[1]), .c2(cin[2]), .c3(cin[3]), .x(three));
  fourDecoder fourdecoder_1 (.c0(cin[0]), .c1(cin[1]), .c2(cin[2]), .c3(cin[3]), .x(four));
  fiveDecoder fivedecoder_1 (.c0(cin[0]), .c1(cin[1]), .c2(cin[2]), .c3(cin[3]), .x(five));
  sixDecoder sixdecoder_1 (.c0(cin[0]), .c1(cin[1]), .c2(cin[2]), .c3(cin[3]), .x(six));
endmodule

module zeroDecoder (
  input  c0,
  input  c1,
  input  c2,
  input  c3,
  output x
);

  wire and_1_out, and_2_out, and_3_out, and_4_out, and_5_out, and_6_out, not_1_out, not_2_out, not_3_out,
       not_4_out;

  not not_1 (not_1_out, c0);
  not not_2 (not_2_out, c1);
  not not_3 (not_3_out, c2);
  not not_4 (not_4_out, c3);
  and and_1 (and_1_out, not_3_out, not_1_out);
  and and_2 (and_2_out, not_4_out, c1);
  and and_3 (and_3_out, not_4_out, c2, c0);
  and and_4 (and_4_out, c2, c1);
  and and_5 (and_5_out, c3, not_1_out);
  and and_6 (and_6_out, c3, not_3_out, not_2_out);
  or or_1 (x, and_1_out, and_2_out, and_3_out, and_4_out, and_5_out, and_6_out);
endmodule

module oneDecoder (
  input  c0,
  input  c1,
  input  c2,
  input  c3,
  output x
);

  wire and_1_out, and_2_out, and_3_out, and_4_out, and_5_out, not_1_out, not_2_out, not_3_out, not_4_out;

  not not_1 (not_1_out, c0);
  not not_2 (not_2_out, c1);
  not not_3 (not_3_out, c2);
  not not_4 (not_4_out, c3);
  and and_1 (and_1_out, not_4_out, not_2_out, not_1_out);
  and and_2 (and_2_out, not_4_out, c1, c0);
  and and_3 (and_3_out, not_4_out, not_3_out);
  and and_4 (and_4_out, c3, not_2_out, c0);
  and and_5 (and_5_out, c3, not_3_out, not_1_out);
  or or_1 (x, and_1_out, and_2_out, and_3_out, and_4_out, and_5_out);
endmodule

module twoDecoder (
  input  c0,
  input  c1,
  input  c2,
  input  c3,
  output x
);

  wire and_1_out, and_2_out, and_3_out, and_4_out, and_5_out, not_1_out, not_2_out, not_3_out, not_4_out;

  not not_1 (not_1_out, c0);
  not not_2 (not_2_out, c1);
  not not_3 (not_3_out, c2);
  not not_4 (not_4_out, c3);
  and and_1 (and_1_out, not_4_out, not_2_out, not_1_out);
  and and_2 (and_2_out, not_4_out, c1, c0);
  and and_3 (and_3_out, not_4_out, c2, c1);
  and and_4 (and_4_out, not_2_out, c0);
  and and_5 (and_5_out, c3, not_3_out);
  or or_1 (x, and_1_out, and_2_out, and_3_out, and_4_out, and_5_out);
endmodule

module threeDecoder (
  input  c0,
  input  c1,
  input  c2,
  input  c3,
  output x
);

  wire and_1_out, and_2_out, and_3_out, and_4_out, and_5_out, not_1_out, not_2_out, not_3_out, not_4_out;

  not not_1 (not_1_out, c0);
  not not_2 (not_2_out, c1);
  not not_3 (not_3_out, c2);
  not not_4 (not_4_out, c3);
  and and_1 (and_1_out, not_4_out, not_3_out, not_1_out);
  and and_2 (and_2_out, c2, not_2_out, c0);
  and and_3 (and_3_out, not_3_out, c1, c0);
  and and_4 (and_4_out, c2, c1, not_1_out);
  and and_5 (and_5_out, c3, not_2_out);
  or or_1 (x, and_1_out, and_2_out, and_3_out, and_4_out, and_5_out);
endmodule

module fourDecoder (
  input  c0,
  input  c1,
  input  c2,
  input  c3,
  output x
);

  wire and_1_out, and_2_out, and_3_out, and_4_out, not_1_out, not_2_out, not_3_out, not_4_out;

  not not_1 (not_1_out, c0);
  not not_2 (not_2_out, c1);
  not not_3 (not_3_out, c2);
  not not_4 (not_4_out, c3);
  and and_1 (and_1_out, not_3_out, not_2_out, not_1_out);
  and and_2 (and_2_out, c1, not_1_out);
  and and_3 (and_3_out, c3, c2);
  and and_4 (and_4_out, c3, c1);
  or or_1 (x, and_1_out, and_2_out, and_3_out, and_4_out);
endmodule

module fiveDecoder (
  input  c0,
  input  c1,
  input  c2,
  input  c3,
  output x
);

  wire and_1_out, and_2_out, and_3_out, and_4_out, and_5_out, not_1_out, not_2_out, not_3_out, not_4_out;

  not not_1 (not_1_out, c0);
  not not_2 (not_2_out, c1);
  not not_3 (not_3_out, c2);
  not not_4 (not_4_out, c3);
  and and_1 (and_1_out, not_4_out, c2, not_2_out);
  and and_2 (and_2_out, c2, c1, not_1_out);
  and and_3 (and_3_out, not_2_out, not_1_out);
  and and_4 (and_4_out, c3, not_3_out);
  and and_5 (and_5_out, c3, c1);
  or or_1 (x, and_1_out, and_2_out, and_3_out, and_4_out, and_5_out);
endmodule

module sixDecoder (
  input  c0,
  input  c1,
  input  c2,
  input  c3,
  output x
);

  wire and_1_out, and_2_out, and_3_out, and_4_out, and_5_out, not_1_out, not_2_out, not_3_out, not_4_out;

  not not_1 (not_1_out, c0);
  not not_2 (not_2_out, c1);
  not not_3 (not_3_out, c2);
  not not_4 (not_4_out, c3);
  and and_1 (and_1_out, not_4_out, c2, not_2_out);
  and and_2 (and_2_out, c3, c2, c0);
  and and_3 (and_3_out, not_4_out, not_3_out, c1);
  and and_4 (and_4_out, c3, not_3_out);
  and and_5 (and_5_out, c1, not_1_out);
  or or_1 (x, and_1_out, and_2_out, and_3_out, and_4_out, and_5_out);
endmodule
