// Logisim project Part3.circ as structural Verilog: 7 circuits, main circuit main
module main (
  input  SW0,
  input  SW1,
  input  SW2,
  input  KEY0,
  input  KEY1
);

  wire Clk_out, ratedivider_1_clkout, shiftregister_1_ledr;
  wire [15:0] lut_1_out_2;

  Clock Clk (.out(Clk_out));
  LUT lut_1 (.cin({SW2, SW1, SW0}), .out_2(lut_1_out_2));
  RateDivider ratedivider_1 (.ClkIn(Clk_out), .ClkOut(ratedivider_1_clkout));
  ShiftRegister shiftregister_1 (
    .load_val(lut_1_out_2), .reset(KEY0), .enable(ratedivider_1_clkout), .displayLED(KEY1),
    .LEDR(shiftregister_1_ledr));
  LED LEDR (.in(shiftregister_1_ledr));
endmodule

module RateDivider (
  input  ClkIn,
  output ClkOut
);

  wire d_ff_1_q, d_ff_1_qn, d_ff_2_q, d_ff_2_qn, d_ff_3_qn;

  D_Flip_Flop d_ff_1 (.D(d_ff_1_qn), .clk(ClkIn), .Q(d_ff_1_q), .Qn(d_ff_1_qn));  // open: preset, reset
  D_Flip_Flop d_ff_2 (.D(d_ff_2_qn), .clk(d_ff_1_q), .Q(d_ff_2_q), .Qn(d_ff_2_qn));  // open: preset, reset
  D_Flip_Flop d_ff_3 (.D(d_ff_3_qn), .clk(d_ff_2_q), .Q(ClkOut), .Qn(d_ff_3_qn));  // open: preset, reset
endmodule

module LUT (
  input  [2:0] cin,
  output [15:0] out_2
);

  Multiplexer #(.enable("false"), .select(3), .width(16)) multiplexer_1 (
    .in0(16'ha800), .in1(16'he000), .in2(16'hae00), .in3(16'hab80), .in4(16'hbb80), .in5(16'heae0),
    .in6(16'hebb8), .in7(16'heea0), .out(out_2), .sel(cin));
endmodule

module ShiftRegister (
  input  [15:0] load_val,
  input  reset,
  input  enable,
  input  displayLED,
  output LEDR
);

  wire onebitshifter_1_cout, onebitshifter_2_cout, onebitshifter_3_cout, onebitshifter_4_cout,
       onebitshifter_5_cout, onebitshifter_6_cout, onebitshifter_7_cout, onebitshifter_8_cout,
       onebitshifter_9_cout, onebitshifter_10_cout, onebitshifter_11_cout, onebitshifter_12_cout,
       onebitshifter_13_cout, onebitshifter_14_cout, onebitshifter_15_cout, onebitshifter_16_cout;

  OneBitShifter onebitshifter_1 (
    .load_val(load_val[0]), .cin(1'b0), .shift(displayLED), .Clk(enable), .load_n(displayLED), .reset(reset),
    .cout(onebitshifter_1_cout));
  OneBitShifter onebitshifter_2 (
    .load_val(load_val[1]), .cin(onebitshifter_1_cout), .shift(displayLED), .Clk(enable),
    .load_n(displayLED), .reset(reset), .cout(onebitshifter_2_cout));
  OneBitShifter onebitshifter_3 (
    .load_val(load_val[2]), .cin(onebitshifter_2_cout), .shift(displayLED), .Clk(enable),
    .load_n(displayLED), .reset(reset), .cout(onebitshifter_3_cout));
  OneBitShifter onebitshifter_4 (
    .load_val(load_val[3]), .cin(onebitshifter_3_cout), .shift(displayLED), .Clk(enable),
    .load_n(displayLED), .reset(reset), .cout(onebitshifter_4_cout));
  OneBitShifter onebitshifter_5 (
    .load_val(load_val[4]), .cin(onebitshifter_4_cout), .shift(displayLED), .Clk(enable),
    .load_n(displayLED), .reset(reset), .cout(onebitshifter_5_cout));
  OneBitShifter onebitshifter_6 (
    .load_val(load_val[5]), .cin(onebitshifter_5_cout), .shift(displayLED), .Clk(enable),
    .load_n(displayLED), .reset(reset), .cout(onebitshifter_6_cout));
  OneBitShifter onebitshifter_7 (
    .load_val(load_val[6]), .cin(onebitshifter_6_cout), .shift(displayLED), .Clk(enable),
    .load_n(displayLED), .reset(reset), .cout(onebitshifter_7_cout));
  OneBitShifter onebitshifter_8 (
    .load_val(load_val[7]), .cin(onebitshifter_7_cout), .shift(displayLED), .Clk(enable),
    .load_n(displayLED), .reset(reset), .cout(onebitshifter_8_cout));
  OneBitShifter onebitshifter_9 (
    .load_val(load_val[8]), .cin(onebitshifter_8_cout), .shift(displayLED), .Clk(enable),
    .load_n(displayLED), .reset(reset), .cout(onebitshifter_9_cout));
  OneBitShifter onebitshifter_10 (
    .load_val(load_val[9]), .cin(onebitshifter_9_cout), .shift(displayLED), .Clk(enable),
    .load_n(displayLED), .reset(reset), .cout(onebitshifter_10_cout));
  OneBitShifter onebitshifter_11 (
    .load_val(load_val[10]), .cin(onebitshifter_10_cout), .shift(displayLED), .Clk(enable),
    .load_n(displayLED), .reset(reset), .cout(onebitshifter_11_cout));
  OneBitShifter onebitshifter_12 (
    .load_val(load_val[11]), .cin(onebitshifter_11_cout), .shift(displayLED), .Clk(enable),
    .load_n(displayLED), .reset(reset), .cout(onebitshifter_12_cout));
  OneBitShifter onebitshifter_13 (
    .load_val(load_val[12]), .cin(onebitshifter_12_cout), .shift(displayLED), .Clk(enable),
    .load_n(displayLED), .reset(reset), .cout(onebitshifter_13_cout));
  OneBitShifter onebitshifter_14 (
    .load_val(load_val[13]), .cin(onebitshifter_13_cout), .shift(displayLED), .Clk(enable),
    .load_n(displayLED), .reset(reset), .cout(onebitshifter_14_cout));
  OneBitShifter onebitshifter_15 (
    .load_val(load_val[14]), .cin(onebitshifter_14_cout), .shift(displayLED), .Clk(enable),
    .load_n(displayLED), .reset(reset), .cout(onebitshifter_15_cout));
  OneBitShifter onebitshifter_16 (
    .load_val(load_val[15]), .cin(onebitshifter_15_cout), .shift(displayLED), .Clk(enable),
    .load_n(displayLED), .reset(reset), .cout(onebitshifter_16_cout));
  and and_1 (LEDR, onebitshifter_16_cout, displayLED);
endmodule

module OneBitShifter (
  input  load_val,
  input  cin,
  input  shift,
  input  Clk,
  input  load_n,
  input  reset,
  output cout
);

  wire mux2to1_1_m, mux2to1_2_m;

  mux2to1 mux2to1_1 (.x(cout), .y(cin), .s(shift), .m(mux2to1_1_m));
  mux2to1 mux2to1_2 (.x(load_val), .y(mux2to1_1_m), .s(load_n), .m(mux2to1_2_m));
  D_Flip_Flop d_ff_1 (.D(mux2to1_2_m), .clk(Clk), .Q(cout), .reset(reset));  // open: Qn, preset
endmodule

module mux2to1 (
  input  x,
  input  y,
  input  s,
  output m
);

  Multiplexer #(.enable("false")) multiplexer_1 (.in0(x), .in1(y), .out(m), .sel(s));
endmodule

module signextender (
  input  sign_in,
  input  ASR,
  output sign,
  output cout,
  output sign_value
);

  mux2to1 mux2to1_1 (.x(1'b0), .y(sign_in), .s(ASR), .m(sign));
  mux2to1 mux2to1_2 (.x(sign_in), .y(1'b0), .s(ASR), .m(cout));

  assign sign_value = sign_in;
endmodule
