// Logisim project Part1.circ as structural Verilog: 1 circuit, main circuit main
module main (
  input  in_1
);

  wire clock_1_out, not_1_out, not_2_out;
  wire [3:0] counter_2_q, ram_1_dout;
  wire [4:0] counter_1_q;

  Clock clock_1 (.out(clock_1_out));
  Counter #(.max('h1f), .width(5)) counter_1 (
    .load(not_1_out), .up(1'b1), .clk(clock_1_out), .Q(counter_1_q));  // open: clr, count, D, carry
  not not_1 (not_1_out, 1'b1);
  not not_2 (not_2_out, 1'b1);
  Counter #(.max('hf), .width(4)) counter_2 (
    .load(not_2_out), .up(1'b1), .clk(clock_1_out), .Q(counter_2_q));  // open: clr, count, D, carry
  RAM #(.addrWidth(5), .dataWidth(4)) ram_1 (
    .addr(counter_1_q), .we(in_1), .oe(in_1), .clk(clock_1_out), .din(counter_2_q), .dout(ram_1_dout));
  Hex_Digit_Display hex_digit_display_1 (.value(ram_1_dout));  // open: dp
endmodule
