// Logisim project Part2.circ as structural Verilog: 3 circuits, main circuit FSM
module main (
  input  reset,
  input  Enable,
  input  [6:0] X,
  input  [6:0] Y
);

  wire Clk_out, fsm_1_enable_out, rgb_video_1_p3;
  wire [3:0] fsm_1_x, fsm_1_y;
  wire [6:0] rgb_video_1_p4, rgb_video_1_p5;
  wire [23:0] rgb_video_1_p6;

  Clock Clk (.out(Clk_out));
  FSM fsm_1 (.reset(reset), .Enable(Enable), .Clk(Clk_out), .X(fsm_1_x), .Y(fsm_1_y), .enable_out(fsm_1_enable_out));
  // RGB_Video rgb_video_1: pin names not known; wires that end beside it: reset, Clk_out, rgb_video_1_p3, rgb_video_1_p4, rgb_video_1_p5, rgb_video_1_p6
  datapath datapath_1 (
    .Enable_in(fsm_1_enable_out), .X_in(X), .Y_in(Y), .Clk(Clk_out), .X_change(fsm_1_x), .Y_change(fsm_1_y),
    .Enable_out(rgb_video_1_p3), .X_out(rgb_video_1_p4), .Y_out(rgb_video_1_p5), .RGB(rgb_video_1_p6));
endmodule

module FSM (
  input  reset,
  input  Enable,
  input  Clk,
  output [3:0] X,
  output [3:0] Y,
  output enable_out
);

  wire not_1_out;
  wire [8:0] counter_1_q;
  wire [8:8] subtractor_1_out;

  not not_1 (not_1_out, Enable);
  Counter #(.max('h100), .width(9)) counter_1 (
    .clr(reset), .load(not_1_out), .up(1'b1), .clk(Clk), .D(counter_1_q), .Q(counter_1_q));  // open: count, carry
  Subtractor #(.width(9)) subtractor_1 (
    .a(counter_1_q), .b(9'h1), .out({subtractor_1_out[8], Y, X}));  // open: bin, bout
  or or_1 (enable_out, counter_1_q[0], counter_1_q[1], counter_1_q[2], counter_1_q[3], counter_1_q[4], counter_1_q[5], counter_1_q[6], counter_1_q[7], counter_1_q[8]);
endmodule

module datapath (
  input  Enable_in,
  input  [6:0] X_in,
  input  [6:0] Y_in,
  input  Clk,
  input  [3:0] X_change,
  input  [3:0] Y_change,
  output Enable_out,
  output [6:0] X_out,
  output [6:0] Y_out,
  output [23:0] RGB
);

  wire not_1_out;
  wire [6:0] bit_extender_1_out, bit_extender_2_out, register_1_q, register_2_q;

  not not_1 (not_1_out, Enable_in);
  Register #(.width(7)) register_1 (.D(X_in), .en(not_1_out), .clk(Clk), .Q(register_1_q));  // open: clr
  Register #(.width(7)) register_2 (.D(Y_in), .en(not_1_out), .clk(Clk), .Q(register_2_q));  // open: clr
  assign bit_extender_1_out = {{3{1'b0}}, X_change};  // Bit_Extender bit_extender_1
  assign bit_extender_2_out = {{3{1'b0}}, Y_change};  // Bit_Extender bit_extender_2
  Adder #(.width(7)) adder_1 (.a(register_1_q), .b(bit_extender_1_out), .out(X_out));  // open: cin, cout
  Adder #(.width(7)) adder_2 (.a(register_2_q), .b(bit_extender_2_out), .out(Y_out));  // open: cin, cout

  assign Enable_out = Enable_in;
  assign RGB = 24'hff00;
endmodule
